# Fritzing sketch ir_connections_with_arduino_JsoWN4jZx9 (saved by Fritzing 0.9.3b)
breadboards: 1

parts:
  Part1 = Arduino Uno (Rev3)
  J1 = Infrared Proximity Sensor
  J2 = Infrared Proximity Sensor
  J3 = Infrared Proximity Sensor

nets:
  N1: Part1.A0, J2.Vout
  N2: Part1.A2, J3.Vout
  N3: Part1.A5/SCL, J1.Vout
  VCC: Part1.3V3, J1.Vcc, J2.Vcc, J3.Vcc
  GND: Part1.GND, J1.GND, J2.GND, J3.GND
